// Logisim project Lab01_Mux21.circ as structural Verilog: 1 circuit, main circuit main
module main (
  input  Sel,
  input  In1,
  input  In0,
  output Out1
);

  wire and_1_out, and_2_out, not_1_out, not_2_out;

  not not_1 (not_1_out, Sel);
  not not_2 (not_2_out, not_1_out);
  and and_1 (and_1_out, not_2_out, In1);
  or or_1 (Out1, and_1_out, and_2_out);
  and and_2 (and_2_out, not_1_out, In0);

  // Notes on the sheet:
  //   Kadirzhan Lutfullayev
  //   Lab 1
  //   15.02.2025
endmodule
