// Logisim project Lab05_DFlipFlop.circ as structural Verilog: 7 circuits, main circuit main
module main (
  input  [2:0] in_1,
  input  rst
);

  wire clk_out;
  wire [3:0] universal_1_counter;

  Clock #(.highDuration(4), .lowDuration(4)) clk (.out(clk_out));
  Clock sysclk ();  // open: out
  // Probe on universal_1_counter
  universal universal_1 (.sel(in_1), .clk(clk_out), .rst(rst), .counter(universal_1_counter));
  Hex_Digit_Display hex_digit_display_1 (.value(universal_1_counter));  // open: dp

  // Notes on the sheet:
  //   0 - up
  //   1 - down
  //   2 - decade
  //   3 - ring
  //   4 - johnson
endmodule

module up_counter (
  input  clk,
  input  rst,
  output [3:0] up
);

  wire d_ff_1_qn, d_ff_2_qn, d_ff_3_qn, d_ff_4_qn;

  D_Flip_Flop d_ff_1 (.D(d_ff_1_qn), .clk(clk), .Q(up[0]), .Qn(d_ff_1_qn), .reset(rst));  // open: preset
  D_Flip_Flop d_ff_2 (.D(d_ff_2_qn), .clk(d_ff_1_qn), .Q(up[1]), .Qn(d_ff_2_qn), .reset(rst));  // open: preset
  D_Flip_Flop d_ff_3 (.D(d_ff_3_qn), .clk(d_ff_2_qn), .Q(up[2]), .Qn(d_ff_3_qn), .reset(rst));  // open: preset
  D_Flip_Flop d_ff_4 (.D(d_ff_4_qn), .clk(d_ff_3_qn), .Q(up[3]), .Qn(d_ff_4_qn), .reset(rst));  // open: preset
endmodule

module down_counter (
  input  clk,
  input  rst,
  output [3:0] down
);

  wire d_ff_1_qn, d_ff_2_qn, d_ff_3_qn, d_ff_4_qn;

  D_Flip_Flop d_ff_1 (.D(d_ff_1_qn), .clk(clk), .Q(down[0]), .Qn(d_ff_1_qn), .preset(rst));  // open: reset
  D_Flip_Flop d_ff_2 (.D(d_ff_2_qn), .clk(down[0]), .Q(down[1]), .Qn(d_ff_2_qn), .preset(rst));  // open: reset
  D_Flip_Flop d_ff_3 (.D(d_ff_3_qn), .clk(down[1]), .Q(down[2]), .Qn(d_ff_3_qn), .preset(rst));  // open: reset
  D_Flip_Flop d_ff_4 (.D(d_ff_4_qn), .clk(down[2]), .Q(down[3]), .Qn(d_ff_4_qn), .preset(rst));  // open: reset
endmodule

module decade_counter (
  input  clk,
  input  rst,
  output [3:0] decade
);

  wire and_1_out, d_ff_1_qn, d_ff_2_qn, d_ff_3_qn, d_ff_4_qn, or_1_out;

  D_Flip_Flop d_ff_1 (.D(d_ff_1_qn), .clk(clk), .Q(decade[0]), .Qn(d_ff_1_qn), .reset(or_1_out));  // open: preset
  and and_1 (and_1_out, decade[1], decade[3]);
  or or_1 (or_1_out, rst, and_1_out);
  D_Flip_Flop d_ff_2 (.D(d_ff_2_qn), .clk(d_ff_1_qn), .Q(decade[1]), .Qn(d_ff_2_qn), .reset(or_1_out));  // open: preset
  D_Flip_Flop d_ff_3 (.D(d_ff_3_qn), .clk(d_ff_2_qn), .Q(decade[2]), .Qn(d_ff_3_qn), .reset(or_1_out));  // open: preset
  D_Flip_Flop d_ff_4 (.D(d_ff_4_qn), .clk(d_ff_3_qn), .Q(decade[3]), .Qn(d_ff_4_qn), .reset(or_1_out));  // open: preset
endmodule

module ring_counter (
  input  clk,
  input  rst,
  output [3:0] ring
);

  D_Flip_Flop d_ff_1 (.D(ring[3]), .clk(clk), .Q(ring[0]), .preset(rst));  // open: Qn, reset
  D_Flip_Flop d_ff_2 (.D(ring[0]), .clk(clk), .Q(ring[1]), .reset(rst));  // open: Qn, preset
  D_Flip_Flop d_ff_3 (.D(ring[1]), .clk(clk), .Q(ring[2]), .reset(rst));  // open: Qn, preset
  D_Flip_Flop d_ff_4 (.D(ring[2]), .clk(clk), .Q(ring[3]), .reset(rst));  // open: Qn, preset
endmodule

module johnson_counter (
  input  clk,
  input  rst,
  output [3:0] johnson
);

  wire d_ff_4_qn;

  D_Flip_Flop d_ff_1 (.D(d_ff_4_qn), .clk(clk), .Q(johnson[0]), .preset(rst));  // open: Qn, reset
  D_Flip_Flop d_ff_2 (.D(johnson[0]), .clk(clk), .Q(johnson[1]), .reset(rst));  // open: Qn, preset
  D_Flip_Flop d_ff_3 (.D(johnson[1]), .clk(clk), .Q(johnson[2]), .reset(rst));  // open: Qn, preset
  D_Flip_Flop d_ff_4 (.D(johnson[2]), .clk(clk), .Q(johnson[3]), .Qn(d_ff_4_qn), .reset(rst));  // open: preset
endmodule

module universal (
  input  [2:0] sel,
  input  clk,
  input  rst,
  output [3:0] counter
);

  wire [3:0] decade_counter_1_decade, down_counter_1_down, johnson_counter_1_johnson, ring_counter_1_ring,
       up_counter_1_up;

  up_counter up_counter_1 (.clk(clk), .rst(rst), .up(up_counter_1_up));
  down_counter down_counter_1 (.clk(clk), .rst(rst), .down(down_counter_1_down));
  decade_counter decade_counter_1 (.clk(clk), .rst(rst), .decade(decade_counter_1_decade));
  ring_counter ring_counter_1 (.clk(clk), .rst(rst), .ring(ring_counter_1_ring));
  johnson_counter johnson_counter_1 (.clk(clk), .rst(rst), .johnson(johnson_counter_1_johnson));
  Multiplexer #(.select(3), .width(4)) multiplexer_1 (
    .in0(up_counter_1_up), .in1(down_counter_1_down), .in2(decade_counter_1_decade),
    .in3(ring_counter_1_ring), .in4(johnson_counter_1_johnson), .out(counter), .sel(sel));  // open: in5, in6, in7

  // Notes on the sheet:
  //   0 - up
  //   1 - down
  //   2 - decade
  //   3 - ring
  //   4 - johnson
endmodule
